// Logisim project PROJECT_X8.circ as structural Verilog: 7 circuits, main circuit main
module main (
  input  in_1,
  input  in_2
);

  wire dipswitch_1_sw1, dipswitch_1_sw2, dipswitch_1_sw3, dipswitch_1_sw4, dipswitch_1_sw5, dipswitch_1_sw6,
       dipswitch_1_sw7, dipswitch_1_sw8, dipswitch_2_p1, dipswitch_2_p2, dipswitch_2_p3, dipswitch_2_p4,
       dipswitch_2_p5, dipswitch_2_p6, dipswitch_2_p7, dipswitch_2_p8, i8bit_adder_1_s0, i8bit_adder_1_s1,
       i8bit_adder_1_s2, i8bit_adder_1_s3, i8bit_adder_1_s4, i8bit_adder_1_s5, i8bit_adder_1_s6,
       i8bit_adder_1_s7, i8bit_register_1_t0, i8bit_register_1_t1, i8bit_register_1_t2, i8bit_register_1_t3,
       i8bit_register_1_t4, i8bit_register_1_t5, i8bit_register_1_t6, i8bit_register_1_t7;

  DipSwitch dipswitch_1 (
    .sw1(dipswitch_1_sw1), .sw2(dipswitch_1_sw2), .sw3(dipswitch_1_sw3), .sw4(dipswitch_1_sw4),
    .sw5(dipswitch_1_sw5), .sw6(dipswitch_1_sw6), .sw7(dipswitch_1_sw7), .sw8(dipswitch_1_sw8));
  // DipSwitch dipswitch_2: pin names not known; wires that end beside it: dipswitch_2_p1, dipswitch_2_p2, dipswitch_2_p3, dipswitch_2_p4, dipswitch_2_p5, dipswitch_2_p6, dipswitch_2_p7, dipswitch_2_p8
  I8bit_adder i8bit_adder_1 (
    .a7(dipswitch_2_p8), .a6(dipswitch_2_p7), .a5(dipswitch_2_p6), .a4(dipswitch_2_p5), .a3(dipswitch_2_p4),
    .a2(dipswitch_2_p3), .a1(dipswitch_2_p2), .a0(dipswitch_2_p1), .b7(dipswitch_1_sw8),
    .b6(dipswitch_1_sw7), .b5(dipswitch_1_sw6), .b4(dipswitch_1_sw5), .b3(dipswitch_1_sw4),
    .b2(dipswitch_1_sw3), .b1(dipswitch_1_sw2), .b0(dipswitch_1_sw1), .o_c(1'b0), .s7(i8bit_adder_1_s7),
    .s6(i8bit_adder_1_s6), .s5(i8bit_adder_1_s5), .s4(i8bit_adder_1_s4), .s3(i8bit_adder_1_s3),
    .s2(i8bit_adder_1_s2), .s1(i8bit_adder_1_s1), .s0(i8bit_adder_1_s0));  // open: c
  C416 c416_1 ();  // open: In0, In1, In2, In3, T0, T1, T2, T3, T4, T5, T6, T7, T8, T9, T10, T11, T12, T13, T14, T15
  I8bit_register i8bit_register_1 (
    .We(in_2), .Re(in_1), .b7(i8bit_adder_1_s7), .b6(i8bit_adder_1_s6), .b5(i8bit_adder_1_s5),
    .b4(i8bit_adder_1_s4), .b3(i8bit_adder_1_s3), .b2(i8bit_adder_1_s2), .b1(i8bit_adder_1_s1),
    .b0(i8bit_adder_1_s0), .T7(i8bit_register_1_t7), .T6(i8bit_register_1_t6), .T5(i8bit_register_1_t5),
    .T4(i8bit_register_1_t4), .T3(i8bit_register_1_t3), .T2(i8bit_register_1_t2), .T1(i8bit_register_1_t1),
    .T0(i8bit_register_1_t0));
  LED led_1 (.in(i8bit_register_1_t7));
  LED led_2 (.in(i8bit_register_1_t6));
  LED led_3 (.in(i8bit_register_1_t5));
  LED led_4 (.in(i8bit_register_1_t4));
  LED led_5 (.in(i8bit_register_1_t3));
  LED led_6 (.in(i8bit_register_1_t2));
  LED led_7 (.in(i8bit_register_1_t1));
  LED led_8 (.in(i8bit_register_1_t0));
endmodule

module f_1bit_adder (
  input  a,
  input  b,
  input  o_c,
  output s,
  output c
);

  wire and_1_out, and_2_out, xor_1_out;

  xor xor_1 (xor_1_out, a, b);
  and and_1 (and_1_out, a, b);
  and and_2 (and_2_out, xor_1_out, o_c);
  xor xor_2 (s, a, b, o_c);
  or or_1 (c, and_1_out, and_2_out);
endmodule

module I8bit_adder (
  input  a7,
  input  a6,
  input  a5,
  input  a4,
  input  a3,
  input  a2,
  input  a1,
  input  a0,
  input  b7,
  input  b6,
  input  b5,
  input  b4,
  input  b3,
  input  b2,
  input  b1,
  input  b0,
  input  o_c,
  output c,
  output s7,
  output s6,
  output s5,
  output s4,
  output s3,
  output s2,
  output s1,
  output s0
);

  wire f_1bit_adder_2_c, f_1bit_adder_3_c, f_1bit_adder_4_c, f_1bit_adder_5_c, f_1bit_adder_6_c,
       f_1bit_adder_7_c, f_1bit_adder_8_c;

  f_1bit_adder f_1bit_adder_1 (.a(a7), .b(b7), .o_c(f_1bit_adder_2_c), .s(s7), .c(c));
  f_1bit_adder f_1bit_adder_2 (.a(a6), .b(b6), .o_c(f_1bit_adder_3_c), .s(s6), .c(f_1bit_adder_2_c));
  f_1bit_adder f_1bit_adder_3 (.a(a5), .b(b5), .o_c(f_1bit_adder_4_c), .s(s5), .c(f_1bit_adder_3_c));
  f_1bit_adder f_1bit_adder_4 (.a(a4), .b(b4), .o_c(f_1bit_adder_5_c), .s(s4), .c(f_1bit_adder_4_c));
  f_1bit_adder f_1bit_adder_5 (.a(a3), .b(b3), .o_c(f_1bit_adder_6_c), .s(s3), .c(f_1bit_adder_5_c));
  f_1bit_adder f_1bit_adder_6 (.a(a2), .b(b2), .o_c(f_1bit_adder_7_c), .s(s2), .c(f_1bit_adder_6_c));
  f_1bit_adder f_1bit_adder_7 (.a(a1), .b(b1), .o_c(f_1bit_adder_8_c), .s(s1), .c(f_1bit_adder_7_c));
  f_1bit_adder f_1bit_adder_8 (.a(a0), .b(b0), .o_c(o_c), .s(s0), .c(f_1bit_adder_8_c));
endmodule

module I8bit_subs (
  input  a7,
  input  a6,
  input  a5,
  input  a4,
  input  a3,
  input  a2,
  input  a1,
  input  a0,
  input  b7,
  input  b6,
  input  b5,
  input  b4,
  input  b3,
  input  b2,
  input  b1,
  input  b0,
  input  flag,
  input  CinS,
  input  CinA,
  output CoutA,
  output s7,
  output s6,
  output s5,
  output s4,
  output s3,
  output s2,
  output s1,
  output s0,
  output CoutS
);

  wire i8bit_adder_1_s0, i8bit_adder_1_s1, i8bit_adder_1_s2, i8bit_adder_1_s3, i8bit_adder_1_s4,
       i8bit_adder_1_s5, i8bit_adder_1_s6, i8bit_adder_1_s7, not_1_out, not_2_out, not_3_out, not_4_out,
       not_5_out, not_6_out, not_7_out, not_8_out;

  not not_1 (not_1_out, b7);
  not not_2 (not_2_out, b6);
  not not_3 (not_3_out, b5);
  not not_4 (not_4_out, b4);
  not not_5 (not_5_out, b3);
  not not_6 (not_6_out, b2);
  not not_7 (not_7_out, b1);
  not not_8 (not_8_out, b0);
  I8bit_adder i8bit_adder_1 (
    .a7(not_1_out), .a6(not_2_out), .a5(not_3_out), .a4(not_4_out), .a3(not_5_out), .a2(not_6_out),
    .a1(not_7_out), .a0(not_8_out), .b7(1'b0), .b6(1'b0), .b5(1'b0), .b4(1'b0), .b3(1'b0), .b2(1'b0),
    .b1(1'b0), .b0(flag), .o_c(CinS), .c(CoutS), .s7(i8bit_adder_1_s7), .s6(i8bit_adder_1_s6),
    .s5(i8bit_adder_1_s5), .s4(i8bit_adder_1_s4), .s3(i8bit_adder_1_s3), .s2(i8bit_adder_1_s2),
    .s1(i8bit_adder_1_s1), .s0(i8bit_adder_1_s0));
  I8bit_adder i8bit_adder_2 (
    .a7(a7), .a6(a6), .a5(a5), .a4(a4), .a3(a3), .a2(a2), .a1(a1), .a0(a0), .b7(i8bit_adder_1_s7),
    .b6(i8bit_adder_1_s6), .b5(i8bit_adder_1_s5), .b4(i8bit_adder_1_s4), .b3(i8bit_adder_1_s3),
    .b2(i8bit_adder_1_s2), .b1(i8bit_adder_1_s1), .b0(i8bit_adder_1_s0), .o_c(CinA), .c(CoutA), .s7(s7),
    .s6(s6), .s5(s5), .s4(s4), .s3(s3), .s2(s2), .s1(s1), .s0(s0));
endmodule

module SreL (
  input  \bit ,
  input  We,
  input  Re,
  output R
);

  wire and_1_out, and_2_out, and_3_out, and_4_out, not_1_out, not_2_out, or_1_out;

  not not_1 (not_1_out, \bit );
  and and_1 (and_1_out, not_1_out, We);
  and and_2 (and_2_out, \bit , We);
  not not_2 (not_2_out, and_1_out);
  and and_3 (and_3_out, not_2_out, and_2_out);
  and and_4 (and_4_out, or_1_out, not_2_out);
  or or_1 (or_1_out, and_3_out, and_4_out);
  and and_5 (R, or_1_out, Re);
endmodule

module I8bit_register (
  input  We,
  input  Re,
  input  b7,
  input  b6,
  input  b5,
  input  b4,
  input  b3,
  input  b2,
  input  b1,
  input  b0,
  output T7,
  output T6,
  output T5,
  output T4,
  output T3,
  output T2,
  output T1,
  output T0
);

  SreL srel_1 (.\bit (b7), .We(We), .Re(Re), .R(T7));
  SreL srel_2 (.\bit (b6), .We(We), .Re(Re), .R(T6));
  SreL srel_3 (.\bit (b5), .We(We), .Re(Re), .R(T5));
  SreL srel_4 (.\bit (b4), .We(We), .Re(Re), .R(T4));
  SreL srel_5 (.\bit (b3), .We(We), .Re(Re), .R(T3));
  SreL srel_6 (.\bit (b2), .We(We), .Re(Re), .R(T2));
  SreL srel_7 (.\bit (b1), .We(We), .Re(Re), .R(T1));
  SreL srel_8 (.\bit (b0), .We(We), .Re(Re), .R(T0));
endmodule

module C416 (
  input  In0,
  input  In1,
  input  In2,
  input  In3,
  output T0,
  output T1,
  output T2,
  output T3,
  output T4,
  output T5,
  output T6,
  output T7,
  output T8,
  output T9,
  output T10,
  output T11,
  output T12,
  output T13,
  output T14,
  output T15
);

  wire not_1_out, not_2_out, not_3_out, not_4_out, not_5_out, not_6_out, not_7_out, not_8_out, not_9_out,
       not_10_out, not_11_out, not_12_out, not_13_out, not_14_out, not_15_out, not_16_out, not_17_out,
       not_18_out, not_19_out, not_20_out, not_21_out, not_22_out, not_23_out, not_24_out, not_25_out,
       not_26_out, not_27_out, not_28_out, not_29_out, not_30_out, not_31_out, not_32_out;

  not not_1 (not_1_out, In0);
  not not_2 (not_2_out, In1);
  not not_3 (not_3_out, In2);
  not not_4 (not_4_out, In3);
  not not_5 (not_5_out, In1);
  not not_6 (not_6_out, In2);
  not not_7 (not_7_out, In3);
  not not_8 (not_8_out, In0);
  not not_9 (not_9_out, In2);
  not not_10 (not_10_out, In3);
  not not_11 (not_11_out, In2);
  not not_12 (not_12_out, In3);
  not not_13 (not_13_out, In0);
  not not_14 (not_14_out, In1);
  not not_15 (not_15_out, In3);
  not not_16 (not_16_out, In1);
  not not_17 (not_17_out, In3);
  not not_18 (not_18_out, In0);
  not not_19 (not_19_out, In3);
  not not_20 (not_20_out, In3);
  not not_21 (not_21_out, In0);
  not not_22 (not_22_out, In1);
  not not_23 (not_23_out, In2);
  not not_24 (not_24_out, In1);
  not not_25 (not_25_out, In2);
  not not_26 (not_26_out, In0);
  not not_27 (not_27_out, In2);
  not not_28 (not_28_out, In2);
  not not_29 (not_29_out, In0);
  not not_30 (not_30_out, In1);
  not not_31 (not_31_out, In1);
  not not_32 (not_32_out, In0);
  and and_1 (T0, not_1_out, not_2_out, not_3_out, not_4_out);
  and and_2 (T1, In0, not_5_out, not_6_out, not_7_out);
  and and_3 (T2, not_8_out, In1, not_9_out, not_10_out);
  and and_4 (T3, In0, In1, not_11_out, not_12_out);
  and and_5 (T4, not_13_out, not_14_out, In2, not_15_out);
  and and_6 (T5, In0, not_16_out, In2, not_17_out);
  and and_7 (T6, not_18_out, In1, In2, not_19_out);
  and and_8 (T7, In0, In1, In2, not_20_out);
  and and_9 (T8, not_21_out, not_22_out, not_23_out, In3);
  and and_10 (T9, In0, not_24_out, not_25_out, In3);
  and and_11 (T10, not_26_out, In1, not_27_out, In3);
  and and_12 (T11, In0, In1, not_28_out, In3);
  and and_13 (T12, not_29_out, not_30_out, In2, In3);
  and and_14 (T13, In0, not_31_out, In2, In3);
  and and_15 (T14, not_32_out, In1, In2, In3);
  and and_16 (T15, In0, In1, In2, In3);
endmodule
